# Fritzing sketch IR (saved by Fritzing 0.9.0b)
circuit board: 1.23cm x 0.73cm
breadboards: 1

parts:
  part = female pin header, 3 pins [form="♀ (female)"]
  part_2 = Resistor [tolerance=±5% resistance=220 package=THT]
  part_3 = LED - 5mm [color="Infrared (940nm)" package="5 mm [THT]"]
  part_4 = Resistor [tolerance=±5% resistance=10k package=THT]
  part_5 = LED - 5mm [color="Infrared (940nm)" package="5 mm [THT]"]

nets:
  N1: part.pin1, part_2.Pin_1, part_4.Pin_1
  N2: part.pin2, part_4.Pin_0, part_5.cathode
  N3: part.pin3, part_3.anode, part_5.anode
  N4: part_2.Pin_0, part_3.cathode

notes:
  5v S -
  220
  10K
  IR
