# Fritzing sketch IR_SMD (saved by Fritzing 0.9.3b)
circuit board: 0.957679cm x 0.635cm
breadboards: 1

parts:
  part = female pin header, 3 pins [form="♀ (female)"]
  part_2 = LED - 5mm [color="Infrared (940nm)" package="5 mm [THT]"]
  part_3 = Resistor [tolerance=±5% resistance=220 package="1206 [SMD]"]
  part_4 = Resistor [tolerance=±5% resistance=10k package="0805 [SMD]"]
  part_5 = LED - 5mm [color="Infrared (940nm)" package="5 mm [THT]"]

nets:
  N1: part.pin1, part_3.Pin_1, part_4.Pin_1
  N2: part.pin2, part_2.cathode, part_4.Pin_0
  N3: part.pin3, part_2.anode, part_5.anode
  N4: part_3.Pin_0, part_5.cathode

notes:
  5v S -
  220
  10K
