# Fritzing sketch Bluetooth (saved by Fritzing 0.9.0b)
circuit board: 1.33cm x 0.9cm
breadboards: 1

parts:
  part = female pin header, 4 pins [form="♀ (female)"]
  part_2 = female pin header, 4 pins [form="♀ (female)"]
  part_3 = Resistor [tolerance=±5% resistance=470k package=THT]
  R2 = Resistor [tolerance=±5% resistance=330k package=THT]

nets:
  N1: part.pin1, part_2.pin1
  N2: part.pin2, part_2.pin2, part_3.Pin_1
  N3: part.pin3, part_2.pin3
  N4: part.pin4, part_3.Pin_0, R2.Pin_0
  N5: part_2.pin4, R2.Pin_1

notes:
  RX TX - +
  TX RX - +
