# Fritzing sketch V4b (saved by Fritzing 0.9.2b)
circuit board: 6.13cm x 4.33cm
breadboards: 1

parts:
  J1 = female pin header, 2 pins [form="♀ (female)"]
  J2 = rounded female pin header, 4 pins [form="♀ (female rounded)"]
  J3 = female pin header, 6 pins [form="♀ (female)"]
  J4 = female pin header, 7 pins [form="♀ (female)"]
  J5 = rounded female pin header, 15 pins [form="♀ (female rounded)"]
  J6 = male pin header, 15 pins [form="♂ (male)"]
  J7 = female pin header, 2 pins [form="♀ (female)"]
  J8 = female pin header, 2 pins [form="♀ (female)"]  # not connected
  J10 = female pin header, 2 pins [form="♀ (female)"]
  J11 = rounded female pin header, 15 pins [form="♀ (female rounded)"]
  J12 = male pin header, 15 pins [form="♂ (male)"]
  J13 = female pin header, 6 pins [form="♀ (female)"]
  J14 = female pin header, 7 pins [form="♀ (female)"]
  J15 = female pin header, 2 pins [form="♀ (female)"]
  J16 = female pin header, 2 pins [form="♀ (female)"]
  J17 = female pin header, 2 pins [form="♀ (female)"]
  J18 = female pin header, 2 pins [form="♀ (female)"]
  J19 = female pin header, 2 pins [form="♀ (female)"]
  J20 = female pin header, 2 pins [form="♀ (female)"]
  J21 = rounded female pin header, 4 pins [form="♀ (female rounded)"]
  J22 = female pin header, 3 pins [form="♀ (female)"]
  part = Resistor [tolerance=±5% resistance=2.2k package=THT]
  part_2 = Resistor [tolerance=±5% resistance=1k package=THT]

nets:
  N1: J1.pin1, J1.pin2, J2.pin1, J3.pin3, J4.pin1, J4.pin2, J4.pin3, J4.pin4, J4.pin5, J4.pin6, J4.pin7, J6.pin14, J10.pin1, J10.pin2, J11.pin14, J13.pin3, J21.pin2, J22.pin2, part.Pin_0
  N2: J2.pin2, J5.pin1, J12.pin1, J16.pin1
  N3: J2.pin3, J15.pin2
  N4: J2.pin4, J6.pin12, J11.pin12, J18.pin2, J21.pin1
  N5: J3.pin1, J5.pin8, J12.pin8, J13.pin1
  N6: J3.pin2, J5.pin7, J12.pin7, J13.pin2
  N7: J3.pin4, J13.pin4, J20.pin1
  N8: J3.pin5, J5.pin4, J12.pin4, J13.pin5
  N9: J3.pin6, J5.pin3, J12.pin3, J13.pin6
  N10: J5.pin2, J12.pin2
  N11: J5.pin5, J12.pin5, J15.pin1, J16.pin2
  N12: J5.pin6, J12.pin6
  N13: J5.pin9, J12.pin9
  N14: J5.pin10, J12.pin10
  N15: J5.pin11, J12.pin11
  N16: J5.pin12, J12.pin12
  N17: J5.pin13, J12.pin13
  N18: J5.pin14, J12.pin14, J21.pin3
  N19: J5.pin15, J12.pin15, part.Pin_1, part_2.Pin_0
  N20: J6.pin1, J11.pin1
  N21: J6.pin2, J11.pin2
  N22: J6.pin3, J11.pin3
  N23: J6.pin4, J11.pin4
  N24: J6.pin5, J11.pin5
  N25: J6.pin6, J11.pin6
  N26: J6.pin7, J11.pin7
  N27: J6.pin8, J11.pin8
  N28: J6.pin9, J11.pin9
  N29: J6.pin10, J11.pin10
  N30: J6.pin11, J11.pin11
  N31: J6.pin13, J11.pin13
  N32: J6.pin15, J11.pin15, J19.pin1
  N33: J7.pin1, J7.pin2, J14.pin1, J14.pin2, J14.pin3, J14.pin4, J14.pin5, J14.pin6, J14.pin7, J17.pin1, J20.pin2, J22.pin1
  N34: J17.pin2, J18.pin1, J19.pin2, J22.pin3
  N35: J21.pin4, part_2.Pin_1

notes:
  Thesis Bot 2016
  ++
  --
  +5v  -  IN |
  -
  +
  TX RX RST - 2 3 4 5 6 7 8 9 10 11 12
  VIN GND RST 5V A7 A6 A5 A4 A3 A2 A1 A0 REF 3.3 13
  PCB V4b
  5v or vin(max 12v)
  A7V8A
  3 or 4 Pin Sonar
  pw sw
  L9110
  Arduino Nano
  LM2596
  HC-SR04
  BAT
  Bluetooth
